# Fritzing sketch simon_says (saved by Fritzing 0.9.6b)
breadboards: 1

parts:
  Pico/Pico2_Mod_1 = Raspberry Pi Pico or Pico 2
  S1 = Momentary Switch [package=ksa_sealed_tac_switch]
  S2 = Momentary Switch [package=ksa_sealed_tac_switch]
  S3 = Momentary Switch [package=ksa_sealed_tac_switch]
  S4 = Momentary Switch [package=ksa_sealed_tac_switch]
  S5 = Momentary Switch [package=ksa_sealed_tac_switch]
  LED4 = LED - 3mm [color="Green (555nm)" current=0.030 package="3 mm [THT]"]
  LED3 = LED - 3mm [color="Yellow (585nm)" current=0.030 package="3 mm [THT]"]
  LED2 = LED - 3mm [color="Red (633nm)" current=0.030 package="3 mm [THT]"]
  R3 = Resistor [tolerance=±5% power=0.25 resistance=330 package=THT]
  LED1 = LED - 3mm [color="Blue (430nm)" current=0.030 package="3 mm [THT]"]
  R4 = Resistor [tolerance=±5% power=0.25 resistance=330 package=THT]
  R5 = Resistor [tolerance=±5% power=0.25 resistance=330 package=THT]
  R6 = Resistor [tolerance=±5% power=0.25 resistance=330 package=THT]
  buz1 = Piezo Buzzer
  OLED1 = SSD1306 0.96in 128x64 I2C Monochrome OLED Display  # not connected

nets:
  N1: Pico/Pico2_Mod_1.pin_3, Pico/Pico2_Mod_1.pin_8, Pico/Pico2_Mod_1.pin_13, Pico/Pico2_Mod_1.pin_18, Pico/Pico2_Mod_1.pin_23, Pico/Pico2_Mod_1.pin_28, Pico/Pico2_Mod_1.pin_33, Pico/Pico2_Mod_1.pin_38, S2.1, S2.2, R3.Pin_0, R4.Pin_0, R5.Pin_0, R6.Pin_0, buz1.pin_2
  N2: Pico/Pico2_Mod_1.pin_9, buz1.pin_1
  N3: Pico/Pico2_Mod_1.pin_16, LED1.anode
  N4: Pico/Pico2_Mod_1.pin_17, LED2.anode
  N5: Pico/Pico2_Mod_1.pin_19, LED3.anode
  N6: Pico/Pico2_Mod_1.pin_20, LED4.anode
  N7: S1.1, S1.2
  N8: S1.3, S1.4
  N9: S2.3, S2.4
  N10: S3.1, S3.2
  N11: S3.3, S3.4
  N12: S4.1, S4.2
  N13: S4.3, S4.4
  N14: S5.1, S5.2
  N15: S5.3, S5.4
  N16: LED4.cathode, R6.Pin_1
  N17: LED3.cathode, R5.Pin_1
  N18: LED2.cathode, R4.Pin_1
  N19: R3.Pin_1, LED1.cathode

custom parts:
  Raspberry Pi Pico or Pico 2: Raspberry Pi Pico and Pico 2. Based around the RP2040 and RP2350 microcontrollers respectively, Picos are low cost microcontroller device bringing Raspberry Pi quality, cost, and easy of use to the microcontroller space. Jan 2021, Split part in to two versions: tht (this one) and SMD. This one will drill holes for a .1 in header in pcb to allow plugging in the module as well as providing pads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
  Piezo Buzzer: Part from https://www.nutsvolts.com/magazine/article/november2012_SmileysWorkshop. Breadboard and icon images modified to be 0.3" in spacing and be more similar to the actual physical part.
