# Fritzing sketch musikbox_v2 (saved by Fritzing 0.9.6b)
breadboards: 1

parts:
  S1 = Pushbutton [package="[SMD]"]
  R1 = Resistor [tolerance=±5% power=0.25 resistance=10k package=THT]
  R2 = PHOTOCELL [package=photocell]
  DFRobot_DFPlayer_Mini1 = DFRobot DFPlayer Mini [part_number=DFR0299]
  SP1 = SPEAKER [package=pcb_mount_speaker]
  Mod1 = Raspberry Pi Pico W
  S2 = Pushbutton [package="[SMD]"]

nets:
  N1: S1.Pin_1, S1.Pin_2, Mod1.pin_25
  N2: S1.Pin_3, S1.Pin_4, R1.Pin_0, DFRobot_DFPlayer_Mini1.GND-1, DFRobot_DFPlayer_Mini1.GND-2, Mod1.pin_3, Mod1.pin_8, Mod1.pin_13, Mod1.pin_18, Mod1.pin_23, Mod1.pin_28, Mod1.pin_33, Mod1.pin_38, S2.Pin_1, S2.Pin_2
  N3: R1.Pin_1, R2.P$1, Mod1.pin_34
  N4: R2.P$2, DFRobot_DFPlayer_Mini1.VCC, Mod1.pin_36
  N5: DFRobot_DFPlayer_Mini1.RX, Mod1.pin_21
  N6: DFRobot_DFPlayer_Mini1.TX, Mod1.pin_22
  N7: DFRobot_DFPlayer_Mini1.SPK_1, SP1.-
  N8: DFRobot_DFPlayer_Mini1.SPK_2, SP1.+
  N9: DFRobot_DFPlayer_Mini1.BUSY, Mod1.pin_24
  N10: Mod1.pin_30, S2.Pin_3, S2.Pin_4

custom parts:
  Raspberry Pi Pico W: Raspberry Pi Pico W. Based around the RP2040 microcontroller the Pico W is a low cost microcontroller device bringing Raspberry Pi quality, cost, and easy of use to the microcontroller space. The areas marked KEEPOUT in pcb silkscreen should not have traces running through them to avoid shorts on a soldered in module!
